# Fritzing sketch wiring (saved by Fritzing 0.9.6b)
circuit board: 8.46667cm x 5.64444cm
breadboards: 1

parts:
  Raspberry_Pi_1 = Raspberry Pi 3 [part_number=RPI-3-V1.2]
  S1 = Pushbutton [package="[SMD]"]
  LED1 = LED - 5mm [color="Green (555nm)" current=0.030 package="5 mm [THT]"]
  R1 = Resistor [tolerance=±5% power=0.25 resistance=330 package=THT]
  LED2 = LED - 5mm [color="Red (633nm)" current=0.030 package="5 mm [THT]"]
  R2 = Resistor [tolerance=±5% power=0.25 resistance=330 package=THT]
  Part1 = InvenSense MPU6050

nets (from the breadboard view):
  N1: Raspberry_Pi_1.GPIO2, Part1.SDA
  GND: Raspberry_Pi_1.GPIO3, Raspberry_Pi_1.GND, S1.Pin_1, S1.Pin_2, LED1.cathode, LED2.cathode, Part1.GND, Part1.SCL
  N2: Raspberry_Pi_1.GIPO7, R2.Pin_1
  N3: Raspberry_Pi_1.GIPO8, R1.Pin_1
  N4: Raspberry_Pi_1.GIPO23, S1.Pin_3, S1.Pin_4
  5V: Raspberry_Pi_1.5V, Part1.VCC
  N5: LED1.anode, R1.Pin_0
  N6: LED2.anode, R2.Pin_0
